# Fritzing sketch Sketch (saved by Fritzing 0.9.3b)
circuit board: 8.46667cm x 5.64444cm

parts:
  Componente4 = Arduino Pro Mini v13
  Componente9 = InvenSense MPU6050
  Componente10 = GY-BMEP280 Barometric Pressure Sensor - Breakout
  Componente11 = XBee USB Mini Adapter
  VCC1 = Battery
  S2 = Toggle Switch [package=THT]

nets:
  VCC: Componente4.VCC, Componente9.VCC, Componente10.VCC, Componente11.5V
  GND: Componente4.GND, Componente9.GND, Componente10.GND, Componente11.GND, VCC1.-
  N1: Componente4.A4, Componente9.SDA, Componente10.SDA
  N2: Componente4.A5, Componente9.SCL, Componente10.SCL
  N3: Componente4.RAW, S2.COM
  N4: Componente4.D0/TX, Componente11.TXD
  N5: VCC1.+, S2.L2

custom parts:
  GY-BMEP280 Barometric Pressure Sensor - Breakout: The BME280 is a chip which was originally designed for the next generation of smartphones. It is made up of a very accurate pressure sensor and an associated temperature sensor which helps calibrate the pressure readings. And just for fun they threw in a pretty solid humidity sensor in there as well! So with an I2C connection you have access to enough weather data to make some pretty good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
