# Fritzing sketch Sketch Sensores Unidos (saved by Fritzing 0.9.3b)

parts:
  Componente4 = Arduino Pro Mini v13
  Componente5 = InvenSense MPU6050
  Componente6 = Bluetooth HC-05 Macho
  microSD2 = MicroSD Card Module
  J1 = female pin header, 2 pins [form="♀ (female)"]
  J2 = female pin header, 2 pins [form="♀ (female)"]
  U1 = LIPO-1000mAh [package=lipo-1000]
  U3 = DC-DC_CONVERTER [package=dc-dc_converter]

nets:
  N1: Componente4.VCC, J1.pin2, U3.VOUT
  GND: Componente4.GND, J2.pin1, U3.GND2
  N2: Componente4.A4, Componente5.SDA
  N3: Componente4.A5, Componente5.SCL
  N4: Componente4.D13/SCK, microSD2.SCK
  N5: Componente4.D12/MISO, microSD2.MISO
  N6: Componente4.D11_PWM/MOSI, microSD2.MOSI
  N7: Componente4.D4, Componente4.D3_PWM, microSD2.CS
  N8: Componente4.D1/RX, Componente6.TXD
  N9: Componente4.D0/TX, Componente6.RXD
  VCC: Componente5.VCC, Componente6.VCC, microSD2.VCC, J1.pin1
  GND_2: Componente5.GND, Componente6.GND, microSD2.GND, J2.pin2
  N10: U1.+, U3.VIN
  N11: U1.-, U3.GND1

notes:
  El sensor usador es el Gy-86, sin embargo en fritzing el mas parecido es el MPU6050
  Vcc-------->
  3.3v*------>
  gnd*------>
  scl*------->
  sda*------>
  *que tienen conexion
  Son dos baterias de 3.7v y 1100 mAh
  El reductor usado es el DC-CX8509
  V in
  Gnd in
  V out
  GND out
  HC-06
  SDA->A4
  SCL->A5
